// Logisim project CORG.circ as structural Verilog: 7 circuits, main circuit main
module main (
);

  wire alu_1_zf_out, clk, EX_ALUSrc, EX_Branch, EX_MemRead, EX_MemToReg, EX_MemWrite, EX_RegDst, EX_RegWrite,
       HazardPCWrite, ID_ALUSrc, ID_Branch, ID_MemToReg, ID_MemWrite, ID_RegDst, ID_RegWrite, IDEX_Flush,
       IDEX_Write, IFIDFlush, MEM_Branch, MEM_MemToReg, MEM_MemWrite, MEM_RegWrite, PCSrc, WB_MemToReg,
       WB_RegWrite;
  wire [1:0] ForwardA, ForwardB;
  wire [2:0] EX_ALUOp, EX_DestReg, EX_RS, EX_RT, ID_ALUOp, ID_DestReg, ID_RS, ID_RT, MEM_DestReg, WB_DestReg;
  wire [5:0] IF_ID_Instr_q;
  wire [15:0] adder_1_out, alu_1_r_out, BranchTarget, EX_Imm, EX_RD1, EX_RD2, ID_Imm, IF_ID_PCPlus1_q,
       MEM_ALUResult, MEM_ReadDAta, MEM_WriteData, multiplexer_1_out, programcounter_1_currentpc,
       registerfile_1_readdata1, registerfile_1_readdata2, rom_1_data, WB_ALUResult, WB_Data, WB_ReadDAta;
  wire [15:12] IF_ID_Instr_q_2;

  Clock clock_1 (.out(clk));
  ProgramCounter programcounter_1 (
    .NextPC(multiplexer_1_out), .PCWrite(HazardPCWrite), .clk(clk), .CurrentPC(programcounter_1_currentpc));  // open: Clear
  ForwardingUnit forwardingunit_1 (
    .EX_RS(EX_RS), .EX_RT(EX_RT), .MEM_DestReg(MEM_DestReg), .WB_DestReg(WB_DestReg),
    .MEM_RegWrite(MEM_RegWrite), .WB_RegWrite(WB_RegWrite), .ForwardA(ForwardA), .ForwardB(ForwardB));
  Adder #(.width(16)) adder_1 (.a(programcounter_1_currentpc), .b(16'h1), .out(adder_1_out));  // open: cin, cout
  Multiplexer #(.width(16), .enable("false")) multiplexer_1 (
    .in0(adder_1_out), .in1(BranchTarget), .out(multiplexer_1_out), .sel(PCSrc));
  HazardDetectionUnit hazarddetectionunit_1 (
    .ID_RS(ID_RS), .ID_RT(ID_RT), .EX_RT(EX_RT), .EX_MemRead(EX_MemRead), .Stall(IDEX_Flush));
  assign ID_Imm = {{8{ID_RT[1]}}, {ID_RT[1:0], IF_ID_Instr_q}};  // Bit_Extender bit_extender_1
  ALU alu_1 (
    .IDReadData1(EX_RD1), .IDReadData2(EX_RD2), .IDImmediate(EX_Imm), .EXMEMResult(MEM_ALUResult),
    .MEMWBResult(WB_Data), .ForwardA(ForwardA), .ForwardB(ForwardB), .ALUSrc(EX_ALUSrc), .ALUOp(EX_ALUOp),
    .R_OUT(alu_1_r_out), .ZF_OUT(alu_1_zf_out));
  ROM #(.addrWidth(16), .dataWidth(16)) rom_1 (.addr(programcounter_1_currentpc), .data(rom_1_data));  // open: sel
  not not_1 (HazardPCWrite, IDEX_Flush);
  Register #(.width(16)) IF_ID_Instr (
    .D(rom_1_data), .en(HazardPCWrite), .Q({IF_ID_Instr_q_2, ID_RS, ID_RT, IF_ID_Instr_q}), .clk(clk),
    .clr(IFIDFlush));
  Register #(.width(16)) IF_ID_PCPlus1 (
    .D(adder_1_out), .en(HazardPCWrite), .Q(IF_ID_PCPlus1_q), .clk(clk), .clr(IFIDFlush));
  ControlUnit controlunit_1 (
    .Opcode(IF_ID_Instr_q_2), .RegDst(ID_RegDst), .RegWrite(ID_RegWrite), .ALUSrc(ID_ALUSrc),
    .MemWrite(ID_MemWrite), .MemToReg(ID_MemToReg), .Branch(ID_Branch), .ALUOp(ID_ALUOp));
  Adder #(.width(16)) adder_2 (.a(ID_Imm), .b(IF_ID_PCPlus1_q), .out(BranchTarget));  // open: cin, cout
  Register #(.width(16)) ResultReg (.D(alu_1_r_out), .Q(MEM_ALUResult), .clk(clk));  // open: en, clr
  Multiplexer #(.width(3), .enable("false")) multiplexer_2 (
    .in0(ID_RT), .in1(IF_ID_Instr_q[5:3]), .out(ID_DestReg), .sel(ID_RegDst));
  and and_1 (PCSrc, alu_1_zf_out, ID_Branch);
  Register #(.width(16)) WriteDataReg (.D(EX_RD2), .Q(MEM_WriteData), .clk(clk));  // open: en, clr
  Register #(.width(3)) DestReg1 (.D(EX_DestReg), .Q(MEM_DestReg), .clk(clk));  // open: en, clr
  RegisterFile registerfile_1 (
    .ReadReg1(ID_RS), .ReadReg2(ID_RT), .WriteReg(WB_DestReg), .WriteData(WB_Data), .RegWrite(WB_RegWrite),
    .clk(clk), .ReadData1(registerfile_1_readdata1), .ReadData2(registerfile_1_readdata2));  // open: Clear
  Register #(.width(4)) EXMEM_ControlReg (
    .D({EX_Branch, EX_MemWrite, EX_MemToReg, EX_RegWrite}),
    .Q({MEM_Branch, MEM_MemWrite, MEM_MemToReg, MEM_RegWrite}), .clk(clk));  // open: en, clr
  Register #(.width(16)) ID_EX_AReg (
    .D(registerfile_1_readdata1), .en(IDEX_Write), .Q(EX_RD1), .clk(clk), .clr(IDEX_Flush));
  Register #(.width(16)) ID_EX_BReg (
    .D(registerfile_1_readdata2), .en(IDEX_Write), .Q(EX_RD2), .clk(clk), .clr(IDEX_Flush));
  Register #(.width(16)) ImmReg (.D(ID_Imm), .en(IDEX_Write), .Q(EX_Imm), .clk(clk), .clr(IDEX_Flush));
  RAM #(.addrWidth(16), .dataWidth(16)) ram_1 (
    .addr(MEM_ALUResult), .data(MEM_WriteData), .sel(1'b1), .clk(clk), .ld(MEM_MemWrite), .clr(1'b0));
  Multiplexer #(.width(16), .enable("false")) multiplexer_3 (
    .in0(WB_ALUResult), .in1(WB_ReadDAta), .out(WB_Data), .sel(WB_MemToReg));
  Register #(.width(3)) DestReg (.D(ID_DestReg), .en(IDEX_Write), .Q(EX_DestReg), .clk(clk), .clr(IDEX_Flush));
  Register #(.width(9)) IDEXControlReg (
    .D({ID_ALUOp, ID_Branch, ID_MemToReg, ID_MemWrite, ID_RegDst, ID_ALUSrc, ID_RegWrite}), .en(IDEX_Write),
    .Q({EX_ALUOp, EX_Branch, EX_MemToReg, EX_MemWrite, EX_RegDst, EX_ALUSrc, EX_RegWrite}), .clk(clk),
    .clr(IDEX_Flush));
  Register #(.width(16)) register_1 (.D(MEM_ReadDAta), .Q(WB_ReadDAta), .clk(clk));  // open: en, clr
  Register #(.width(3)) register_2 (.D(ID_RS), .en(IDEX_Write), .Q(EX_RS), .clk(clk), .clr(IDEX_Flush));
  Register #(.width(3)) register_3 (.D(ID_RT), .en(IDEX_Write), .Q(EX_RT), .clk(clk), .clr(IDEX_Flush));
  Register #(.width(16)) register_4 (.D(MEM_ALUResult), .Q(WB_ALUResult), .clk(clk));  // open: en, clr
  Register #(.width(3)) register_5 (.D(MEM_DestReg), .Q(WB_DestReg), .clk(clk));  // open: en, clr
  Register #(.width(2)) register_6 (
    .D({MEM_MemToReg, MEM_RegWrite}), .Q({WB_MemToReg, WB_RegWrite}), .clk(clk));  // open: en, clr

  // Other names for the same wires on the sheet: IFIDWrite = HazardPCWrite
endmodule

module ProgramCounter (
  input  [15:0] NextPC,
  input  PCWrite,
  input  clk,
  input  Clear,
  output [15:0] CurrentPC
);

  Register #(.width(16)) PC (.D(NextPC), .en(PCWrite), .Q(CurrentPC), .clk(clk), .clr(Clear));
endmodule

module ALU (
  input  [15:0] IDReadData1,
  input  [15:0] IDReadData2,
  input  [15:0] IDImmediate,
  input  [15:0] EXMEMResult,
  input  [15:0] MEMWBResult,
  input  [1:0] ForwardA,
  input  [1:0] ForwardB,
  input  ALUSrc,
  input  [2:0] ALUOp,
  output [15:0] R_OUT,
  output ZF_OUT
);

  wire [15:0] adder_1_out, and_1_out, multiplexer_1_out, multiplexer_2_out, multiplexer_3_out, or_1_out,
       subtractor_1_out;

  Multiplexer #(.select(2), .width(16), .enable("false")) multiplexer_1 (
    .in0(IDReadData1), .in1(EXMEMResult), .in2(MEMWBResult), .out(multiplexer_1_out), .sel(ForwardA));  // open: in3
  Multiplexer #(.select(2), .width(16), .enable("false")) multiplexer_2 (
    .in0(IDReadData2), .in1(EXMEMResult), .in2(MEMWBResult), .out(multiplexer_2_out), .sel(ForwardB));  // open: in3
  Multiplexer #(.width(16), .enable("false")) multiplexer_3 (
    .in0(multiplexer_2_out), .in1(IDImmediate), .out(multiplexer_3_out), .sel(ALUSrc));
  Adder #(.width(16)) adder_1 (.a(multiplexer_1_out), .b(multiplexer_3_out), .out(adder_1_out));  // open: cin, cout
  Subtractor #(.width(16)) subtractor_1 (
    .a(multiplexer_1_out), .b(multiplexer_3_out), .out(subtractor_1_out));  // open: bin, bout
  assign and_1_out = multiplexer_1_out & multiplexer_3_out;  // AND_Gate and_1, 16 bits wide
  assign or_1_out = multiplexer_1_out | multiplexer_3_out;  // OR_Gate or_1, 16 bits wide
  Multiplexer #(.select(3), .width(16), .enable("false")) multiplexer_4 (
    .in0(and_1_out), .in1(or_1_out), .in2(adder_1_out), .in6(subtractor_1_out), .out(R_OUT), .sel(ALUOp));  // open: in3, in4, in5, in7
  Comparator #(.width(16)) comparator_1 (.a(R_OUT), .b({16{1'b0}}), .eq(ZF_OUT));  // open: gt, lt
endmodule

module RegisterFile (
  input  [2:0] ReadReg1,
  input  [2:0] ReadReg2,
  input  [2:0] WriteReg,
  input  [15:0] WriteData,
  input  RegWrite,
  input  clk,
  input  Clear,
  output [15:0] ReadData1,
  output [15:0] ReadData2
);

  wire demultiplexer_1_out0, demultiplexer_1_out1, demultiplexer_1_out2, demultiplexer_1_out3,
       demultiplexer_1_out4, demultiplexer_1_out5, demultiplexer_1_out6, demultiplexer_1_out7;
  wire [15:0] R0Q, R1Q, R2Q, R3Q, R4Q, R5Q, R6Q, R7Q;

  Demultiplexer #(.select(3), .enable("false")) demultiplexer_1 (
    .out0(demultiplexer_1_out0), .out1(demultiplexer_1_out1), .out2(demultiplexer_1_out2),
    .out3(demultiplexer_1_out3), .out4(demultiplexer_1_out4), .out5(demultiplexer_1_out5),
    .out6(demultiplexer_1_out6), .out7(demultiplexer_1_out7), .in(RegWrite), .sel(WriteReg));
  Register #(.width(16)) R0 (.D(WriteData), .en(demultiplexer_1_out0), .Q(R0Q), .clk(clk), .clr(Clear));
  Multiplexer #(.select(3), .width(16), .enable("false")) multiplexer_1 (
    .in0(R0Q), .in1(R1Q), .in2(R2Q), .in3(R3Q), .in4(R4Q), .in5(R5Q), .in6(R6Q), .in7(R7Q), .out(ReadData1),
    .sel(ReadReg1));
  Register #(.width(16)) R1 (.D(WriteData), .en(demultiplexer_1_out1), .Q(R1Q), .clk(clk), .clr(Clear));
  Register #(.width(16)) R2 (.D(WriteData), .en(demultiplexer_1_out2), .Q(R2Q), .clk(clk), .clr(Clear));
  Register #(.width(16)) R3 (.D(WriteData), .en(demultiplexer_1_out3), .Q(R3Q), .clk(clk), .clr(Clear));
  Register #(.width(16)) R4 (.D(WriteData), .en(demultiplexer_1_out4), .Q(R4Q), .clk(clk), .clr(Clear));
  Register #(.width(16)) R5 (.D(WriteData), .en(demultiplexer_1_out5), .Q(R5Q), .clk(clk), .clr(Clear));
  Multiplexer #(.select(3), .width(16), .enable("false")) multiplexer_2 (
    .in0(R0Q), .in1(R1Q), .in2(R2Q), .in3(R3Q), .in4(R4Q), .in5(R5Q), .in6(R6Q), .in7(R7Q), .out(ReadData2),
    .sel(ReadReg2));
  Register #(.width(16)) R6 (.D(WriteData), .en(demultiplexer_1_out6), .Q(R6Q), .clk(clk), .clr(Clear));
  Register #(.width(16)) R7 (.D(WriteData), .en(demultiplexer_1_out7), .Q(R7Q), .clk(clk), .clr(Clear));
endmodule

module ControlUnit (
  input  [3:0] Opcode,
  output RegDst,
  output RegWrite,
  output ALUSrc,
  output MemWrite,
  output MemToReg,
  output Branch,
  output [2:0] ALUOp
);

  wire decoder_1_out0, decoder_1_out1, decoder_1_out2, decoder_1_out3, decoder_1_out5;

  or or_1 (RegDst, decoder_1_out0, decoder_1_out1, decoder_1_out2, decoder_1_out3);
  Decoder #(.select(4), .enable("false")) decoder_1 (
    .out0(decoder_1_out0), .out1(decoder_1_out1), .out2(decoder_1_out2), .out3(decoder_1_out3),
    .out4(Branch), .out5(decoder_1_out5), .out10(MemToReg), .out11(MemWrite), .sel(Opcode));  // open: out6, out7, out8, out9, out12, out13, out14, out15
  or or_2 (RegWrite, decoder_1_out0, decoder_1_out1, decoder_1_out2, decoder_1_out3, decoder_1_out5, MemToReg);
  or or_3 (ALUSrc, decoder_1_out5, MemToReg, MemWrite);
  or or_4 (ALUOp[0], decoder_1_out1, Branch, decoder_1_out3);
  or or_5 (ALUOp[1], decoder_1_out2, decoder_1_out3);

  assign ALUOp[2] = 1'b0;
endmodule

module ForwardingUnit (
  input  [2:0] EX_RS,
  input  [2:0] EX_RT,
  input  [2:0] MEM_DestReg,
  input  [2:0] WB_DestReg,
  input  MEM_RegWrite,
  input  WB_RegWrite,
  output [1:0] ForwardA,
  output [1:0] ForwardB
);

  wire and_3_out, and_4_out, comparator_1_eq, comparator_2_eq, comparator_3_eq, comparator_4_eq, not_1_out,
       not_2_out;

  Comparator #(.width(3)) comparator_1 (.a(EX_RT), .b(MEM_DestReg), .eq(comparator_1_eq));  // open: gt, lt
  Comparator #(.width(3)) comparator_2 (.a(EX_RT), .b(WB_DestReg), .eq(comparator_2_eq));  // open: gt, lt
  Comparator #(.width(3)) comparator_3 (.a(EX_RS), .b(MEM_DestReg), .eq(comparator_3_eq));  // open: gt, lt
  and and_1 (ForwardB[1], comparator_1_eq, MEM_RegWrite);
  Comparator #(.width(3)) comparator_4 (.a(EX_RS), .b(WB_DestReg), .eq(comparator_4_eq));  // open: gt, lt
  not not_1 (not_1_out, ForwardB[1]);
  not not_2 (not_2_out, ForwardA[1]);
  and and_2 (ForwardA[1], comparator_3_eq, MEM_RegWrite);
  and and_3 (and_3_out, comparator_2_eq, WB_RegWrite);
  and and_4 (and_4_out, comparator_4_eq, WB_RegWrite);
  and and_5 (ForwardA[0], and_4_out, not_2_out);
  and and_6 (ForwardB[0], and_3_out, not_1_out);
endmodule

module HazardDetectionUnit (
  input  [2:0] ID_RS,
  input  [2:0] ID_RT,
  input  [2:0] EX_RT,
  input  EX_MemRead,
  output Stall
);

  wire comparator_1_eq, comparator_2_eq, or_1_out;

  Comparator #(.width(3)) comparator_1 (.a(ID_RS), .b(EX_RT), .eq(comparator_1_eq));  // open: gt, lt
  Comparator #(.width(3)) comparator_2 (.a(ID_RT), .b(EX_RT), .eq(comparator_2_eq));  // open: gt, lt
  or or_1 (or_1_out, comparator_1_eq, comparator_2_eq);
  and and_1 (Stall, or_1_out, EX_MemRead);
endmodule
